// Logisim project 2003056_LF.circ as structural Verilog
module XOR_2003056 (
  input  [3:0] A,
  input  [3:0] B,
  output [3:0] O
);

  xor xor_1 (O[3], A[3], B[3]);
  xor xor_2 (O[2], A[2], B[2]);
  xor xor_3 (O[1], A[1], B[1]);
  xor xor_4 (O[0], A[0], B[0]);
endmodule

module FA (
  input  a,
  input  b,
  input  Cin,
  output S,
  output Cout
);

  wire and_1_out, and_2_out, xor_1_out;

  xor xor_1 (xor_1_out, a, b);
  xor xor_2 (S, xor_1_out, Cin);
  and and_1 (and_1_out, Cin, xor_1_out);
  and and_2 (and_2_out, a, b);
  or or_1 (Cout, and_1_out, and_2_out);
endmodule

module Add56 (
  input  Sel,
  input  [3:0] A,
  input  [3:0] B,
  output [3:0] O,
  output Carry
);

  wire a0_t, a1_t, a2_t, a3_t, b1_t, b3_t, b_t, fa_1_s, fa_2_cout, fa_2_s, fa_3_cout, fa_3_s, fa_4_s,
       xor_1_out, xor_2_out, xor_3_out;

  xor xor_1 (xor_1_out, b3_t, Sel);
  FA fa_1 (.a(a3_t), .b(xor_1_out), .Cin(fa_2_cout), .S(fa_1_s), .Cout(Carry));
  FA fa_2 (.a(a2_t), .b(xor_2_out), .Cin(fa_3_cout), .S(fa_2_s), .Cout(fa_2_cout));
  xor xor_2 (xor_2_out, b_t, Sel);
  xor xor_3 (xor_3_out, b1_t, Sel);
  FA fa_3 (.a(a1_t), .b(xor_3_out), .Cin(xor_3_out), .S(fa_3_s), .Cout(fa_3_cout));
  // XOR_Gate xor_4 has open pins: in0=b_t, in1=Sel, out=open
  FA fa_4 (.a(a0_t), .Cin(Sel), .S(fa_4_s), .Cout(xor_3_out));  // open: b
endmodule

module RightRotate (
  input  [3:0] A,
  input  [1:0] Shift,
  output [3:0] O
);

  Multiplexer #(.select(2)) multiplexer_1 (.in0(A[3]), .in1(A[0]), .in2(A[1]), .in3(A[2]), .out(O[3]), .sel(Shift));
  Multiplexer #(.select(2)) multiplexer_2 (.in0(A[2]), .in1(A[3]), .in2(A[0]), .in3(A[1]), .out(O[2]), .sel(Shift));
  Multiplexer #(.select(2)) multiplexer_3 (.in0(A[1]), .in1(A[2]), .in2(A[3]), .in3(A[0]), .out(O[1]), .sel(Shift));
  Multiplexer #(.select(2)) multiplexer_4 (.in0(A[0]), .in1(A[1]), .in2(A[2]), .in3(A[3]), .out(O[0]), .sel(Shift));
endmodule

module NOT_2003056 (
  input  [3:0] in_1,
  output [3:0] out_2
);

  not not_1 (out_2[3], in_1[3]);
  not not_2 (out_2[2], in_1[2]);
  not not_3 (out_2[1], in_1[1]);
  not not_4 (out_2[0], in_1[0]);

  // Other names for the same wires on the sheet: A0 = in_1[0]; A1 = in_1[1]; A2 = in_1[2]; A3 = in_1[3];
  //   O0 = out_2[0]; O1 = out_2[1]; O2 = out_2[2]; O3 = out_2[3]
endmodule
