// Logisim project 2003056_LP1.circ as structural Verilog: 2 circuits, main circuit main
module main (
  input  A,
  input  B,
  output OUTPUT
);

  wire and_1_out, and_2_out, not_1_out, not_2_out, or_1_out;

  not not_1 (not_1_out, A);
  not not_2 (not_2_out, B);
  and and_1 (and_1_out, not_1_out, B);
  and and_2 (and_2_out, A, not_2_out);
  or or_1 (or_1_out, and_1_out, and_2_out);
  not not_3 (OUTPUT, or_1_out);

  // Notes on the sheet:
  //   A'B
  //   AB'
  //   A'B+AB'
endmodule

module circit1_2003056 (
  input  in_1,
  input  in_2,
  output out_3
);

  main main_1 (.A(in_1), .B(in_2), .OUTPUT(out_3));
endmodule
