// Logisim project 2t04decoder_prac.circ as structural Verilog: 1 circuit, main circuit main
module main (
  input  A,
  input  B,
  input  E,
  input  in_4,
  input  [1:0] in_5
);

  wire and_1_out, and_2_out, and_3_out, and_4_out, decoder_1_out0, decoder_1_out1, decoder_1_out2,
       decoder_1_out3, not_1_out, not_2_out;

  not not_1 (not_1_out, A);
  not not_2 (not_2_out, B);
  and and_1 (and_1_out, not_1_out, not_2_out, E);
  LED led_1 (.in(and_1_out));
  and and_2 (and_2_out, not_1_out, B, E);
  LED led_2 (.in(and_2_out));
  and and_3 (and_3_out, A, not_2_out, E);
  LED led_3 (.in(and_3_out));
  and and_4 (and_4_out, A, B, E);
  LED led_4 (.in(and_4_out));
  Decoder #(.select(2)) decoder_1 (
    .out0(decoder_1_out0), .out1(decoder_1_out1), .out2(decoder_1_out2), .out3(decoder_1_out3), .sel(in_5),
    .en(in_4));
  LED led_5 (.in(decoder_1_out0));
  LED led_6 (.in(decoder_1_out1));
  LED led_7 (.in(decoder_1_out2));
  LED led_8 (.in(decoder_1_out3));

  // Notes on the sheet:
  //   Y0
  //   Y1
  //   Y2
  //   Y3
endmodule
