// Logisim project Booth_Multiplier_Library.circ as structural Verilog: 6 circuits, main circuit FA
module FA (
  input  a,
  input  b,
  input  Cin,
  output S,
  output Cout
);

  wire and_1_out, and_2_out, xor_1_out;

  xor xor_1 (xor_1_out, a, b);
  xor xor_2 (S, xor_1_out, Cin);
  and and_1 (and_1_out, Cin, xor_1_out);
  and and_2 (and_2_out, a, b);
  or or_1 (Cout, and_1_out, and_2_out);
endmodule

module _1_bit_Adder_Subtractor (
  input  a,
  input  b,
  input  H,
  input  cin,
  input  D,
  output z,
  output Cout
);

  wire adder_1_out, and_1_out, and_2_out, and_3_out, and_4_out, xor_1_out, xor_2_out;

  and and_1 (and_1_out, b, H);
  and and_2 (and_2_out, cin, H);
  xor xor_1 (xor_1_out, a, and_1_out);
  xor xor_2 (xor_2_out, a, D);
  Adder #(.width(1)) adder_1 (.a(b), .b(cin), .out(adder_1_out), .cin(1'b0));  // open: cout
  and and_3 (and_3_out, b, cin);
  xor xor_3 (z, xor_1_out, and_2_out);
  and and_4 (and_4_out, xor_2_out, adder_1_out);
  Adder #(.width(1)) adder_2 (.a(and_4_out), .b(and_3_out), .out(Cout), .cin(1'b0));  // open: cout
endmodule

module Cell_B (
  input  a,
  input  b,
  input  H,
  input  D,
  input  cin,
  output Cout,
  output H_2,
  output D_2,
  output b_2,
  output z
);

  _1_bit_Adder_Subtractor u_1_bit_adder_subtractor_1 (.a(a), .b(b), .H(H), .cin(cin), .D(D), .z(z), .Cout(Cout));

  assign b_2 = b;
  assign D_2 = D;
  assign H_2 = H;
endmodule

module _2x2_booth_MUL (
  input  Y1,
  input  Y0,
  input  X0,
  input  X1,
  output P3,
  output P2,
  output P1,
  output P0
);

  wire cell_b_1_z, cell_b_3_b_2, cell_b_3_cout, cell_b_3_d_2, cell_b_3_h_2, cell_b_3_z, cell_b_4_cout,
       cell_b_4_d_2, cell_b_4_h_2, cell_b_5_b_2, cell_b_5_cout, cell_b_5_d_2, cell_b_5_h_2, cell_b_5_z,
       cell_b_6_cout, cell_b_6_d_2, cell_b_6_h_2, cell_b_7_b_2, cell_b_7_cout, cell_b_7_d_2, cell_b_7_h_2,
       cell_c_1_d, cell_c_1_h, cell_c_2_d, cell_c_2_h;

  Cell_B cell_b_1 (
    .H(cell_b_3_h_2), .D(cell_b_3_d_2), .cin(cell_b_3_cout), .a(1'b0), .b(Y1), .z(cell_b_1_z));  // open: Cout, b_2, D_2, H_2
  Cell_B cell_b_2 (
    .H(cell_b_4_h_2), .D(cell_b_4_d_2), .cin(cell_b_4_cout), .a(cell_b_1_z), .b(cell_b_3_b_2), .z(P3));  // open: Cout, b_2, D_2, H_2
  Cell_B cell_b_3 (
    .Cout(cell_b_3_cout), .H(cell_b_5_h_2), .D(cell_b_5_d_2), .cin(cell_b_5_cout), .a(1'b0), .b(Y1),
    .b_2(cell_b_3_b_2), .z(cell_b_3_z), .D_2(cell_b_3_d_2), .H_2(cell_b_3_h_2));
  Cell_B cell_b_4 (
    .Cout(cell_b_4_cout), .H(cell_b_6_h_2), .D(cell_b_6_d_2), .cin(cell_b_6_cout), .a(cell_b_3_z),
    .b(cell_b_5_b_2), .z(P2), .D_2(cell_b_4_d_2), .H_2(cell_b_4_h_2));  // open: b_2
  Cell_B cell_b_5 (
    .Cout(cell_b_5_cout), .H(cell_b_7_h_2), .D(cell_b_7_d_2), .cin(cell_b_7_cout), .a(1'b0), .b(Y1),
    .b_2(cell_b_5_b_2), .z(cell_b_5_z), .D_2(cell_b_5_d_2), .H_2(cell_b_5_h_2));
  Cell_B cell_b_6 (
    .Cout(cell_b_6_cout), .H(cell_c_2_h), .D(cell_c_2_d), .cin(1'b0), .a(cell_b_5_z), .b(cell_b_7_b_2),
    .z(P1), .D_2(cell_b_6_d_2), .H_2(cell_b_6_h_2));  // open: b_2
  Cell_C cell_c_1 (.x_i_1(1'b0), .x_i(X0), .H(cell_c_1_h), .D(cell_c_1_d));
  Cell_B cell_b_7 (
    .Cout(cell_b_7_cout), .H(cell_c_1_h), .D(cell_c_1_d), .cin(1'b0), .a(1'b0), .b(Y0), .b_2(cell_b_7_b_2),
    .z(P0), .D_2(cell_b_7_d_2), .H_2(cell_b_7_h_2));
  Cell_C cell_c_2 (.x_i_1(X0), .x_i(X1), .H(cell_c_2_h), .D(cell_c_2_d));
endmodule

module Cell_C (
  input  x_i_1,
  input  x_i,
  output H,
  output D
);

  wire not_1_out;

  and and_1 (D, x_i, not_1_out);
  not not_1 (not_1_out, x_i_1);
  xor xor_1 (H, x_i_1, x_i);
endmodule

module _4x4_booth_MUL (
  input  Y3,
  input  Y2,
  input  Y1,
  input  Y0,
  input  X0,
  input  X1,
  input  X2,
  input  X3,
  output P7,
  output P6,
  output P5,
  output P4,
  output P3,
  output P2,
  output P1,
  output P0
);

  wire cell_b_1_z, cell_b_2_z, cell_b_3_z, cell_b_5_b_2, cell_b_5_cout, cell_b_5_d_2, cell_b_5_h_2,
       cell_b_5_z, cell_b_6_b_2, cell_b_6_cout, cell_b_6_d_2, cell_b_6_h_2, cell_b_6_z, cell_b_7_b_2,
       cell_b_7_cout, cell_b_7_d_2, cell_b_7_h_2, cell_b_7_z, cell_b_8_cout, cell_b_8_d_2, cell_b_8_h_2,
       cell_b_9_b_2, cell_b_9_cout, cell_b_9_d_2, cell_b_9_h_2, cell_b_9_z, cell_b_10_b_2, cell_b_10_cout,
       cell_b_10_d_2, cell_b_10_h_2, cell_b_10_z, cell_b_11_b_2, cell_b_11_cout, cell_b_11_d_2,
       cell_b_11_h_2, cell_b_11_z, cell_b_12_cout, cell_b_12_d_2, cell_b_12_h_2, cell_b_13_b_2,
       cell_b_13_cout, cell_b_13_d_2, cell_b_13_h_2, cell_b_13_z, cell_b_14_b_2, cell_b_14_cout,
       cell_b_14_d_2, cell_b_14_h_2, cell_b_14_z, cell_b_15_b_2, cell_b_15_cout, cell_b_15_d_2,
       cell_b_15_h_2, cell_b_15_z, cell_b_16_cout, cell_b_16_d_2, cell_b_16_h_2, cell_b_17_b_2,
       cell_b_17_cout, cell_b_17_d_2, cell_b_17_h_2, cell_b_17_z, cell_b_18_b_2, cell_b_18_cout,
       cell_b_18_d_2, cell_b_18_h_2, cell_b_18_z, cell_b_19_b_2, cell_b_19_cout, cell_b_19_d_2,
       cell_b_19_h_2, cell_b_19_z, cell_b_20_cout, cell_b_20_d_2, cell_b_20_h_2, cell_b_21_b_2,
       cell_b_21_cout, cell_b_21_d_2, cell_b_21_h_2, cell_b_21_z, cell_b_22_b_2, cell_b_22_cout,
       cell_b_22_d_2, cell_b_22_h_2, cell_b_22_z, cell_b_23_b_2, cell_b_23_cout, cell_b_23_d_2,
       cell_b_23_h_2, cell_b_24_b_2, cell_b_24_cout, cell_b_24_d_2, cell_b_24_h_2, cell_b_24_z,
       cell_b_25_b_2, cell_b_25_cout, cell_b_25_d_2, cell_b_25_h_2, cell_b_26_b_2, cell_b_26_cout,
       cell_b_26_d_2, cell_b_26_h_2, cell_c_1_d, cell_c_1_h, cell_c_2_d, cell_c_2_h, cell_c_3_d, cell_c_3_h,
       cell_c_4_d, cell_c_4_h;

  Cell_B cell_b_1 (
    .H(cell_b_5_h_2), .D(cell_b_5_d_2), .cin(cell_b_5_cout), .a(1'b0), .b(Y3), .z(cell_b_1_z));  // open: Cout, b_2, D_2, H_2
  Cell_B cell_b_2 (
    .H(cell_b_6_h_2), .D(cell_b_6_d_2), .cin(cell_b_6_cout), .a(cell_b_1_z), .b(cell_b_5_b_2), .z(cell_b_2_z));  // open: Cout, b_2, D_2, H_2
  Cell_B cell_b_3 (
    .H(cell_b_7_h_2), .D(cell_b_7_d_2), .cin(cell_b_7_cout), .a(cell_b_2_z), .b(cell_b_6_b_2), .z(cell_b_3_z));  // open: Cout, b_2, D_2, H_2
  Cell_B cell_b_4 (
    .H(cell_b_8_h_2), .D(cell_b_8_d_2), .cin(cell_b_8_cout), .a(cell_b_3_z), .b(cell_b_7_b_2), .z(P7));  // open: Cout, b_2, D_2, H_2
  Cell_B cell_b_5 (
    .Cout(cell_b_5_cout), .H(cell_b_9_h_2), .D(cell_b_9_d_2), .cin(cell_b_9_cout), .a(1'b0), .b(Y3),
    .b_2(cell_b_5_b_2), .z(cell_b_5_z), .D_2(cell_b_5_d_2), .H_2(cell_b_5_h_2));
  Cell_B cell_b_6 (
    .Cout(cell_b_6_cout), .H(cell_b_10_h_2), .D(cell_b_10_d_2), .cin(cell_b_10_cout), .a(cell_b_5_z),
    .b(cell_b_9_b_2), .b_2(cell_b_6_b_2), .z(cell_b_6_z), .D_2(cell_b_6_d_2), .H_2(cell_b_6_h_2));
  Cell_B cell_b_7 (
    .Cout(cell_b_7_cout), .H(cell_b_11_h_2), .D(cell_b_11_d_2), .cin(cell_b_11_cout), .a(cell_b_6_z),
    .b(cell_b_10_b_2), .b_2(cell_b_7_b_2), .z(cell_b_7_z), .D_2(cell_b_7_d_2), .H_2(cell_b_7_h_2));
  Cell_B cell_b_8 (
    .Cout(cell_b_8_cout), .H(cell_b_12_h_2), .D(cell_b_12_d_2), .cin(cell_b_12_cout), .a(cell_b_7_z),
    .b(cell_b_11_b_2), .z(P6), .D_2(cell_b_8_d_2), .H_2(cell_b_8_h_2));  // open: b_2
  Cell_B cell_b_9 (
    .Cout(cell_b_9_cout), .H(cell_b_13_h_2), .D(cell_b_13_d_2), .cin(cell_b_13_cout), .a(1'b0), .b(Y3),
    .b_2(cell_b_9_b_2), .z(cell_b_9_z), .D_2(cell_b_9_d_2), .H_2(cell_b_9_h_2));
  Cell_B cell_b_10 (
    .Cout(cell_b_10_cout), .H(cell_b_14_h_2), .D(cell_b_14_d_2), .cin(cell_b_14_cout), .a(cell_b_9_z),
    .b(cell_b_13_b_2), .b_2(cell_b_10_b_2), .z(cell_b_10_z), .D_2(cell_b_10_d_2), .H_2(cell_b_10_h_2));
  Cell_B cell_b_11 (
    .Cout(cell_b_11_cout), .H(cell_b_15_h_2), .D(cell_b_15_d_2), .cin(cell_b_15_cout), .a(cell_b_10_z),
    .b(cell_b_14_b_2), .b_2(cell_b_11_b_2), .z(cell_b_11_z), .D_2(cell_b_11_d_2), .H_2(cell_b_11_h_2));
  Cell_B cell_b_12 (
    .Cout(cell_b_12_cout), .H(cell_b_16_h_2), .D(cell_b_16_d_2), .cin(cell_b_16_cout), .a(cell_b_11_z),
    .b(cell_b_15_b_2), .z(P5), .D_2(cell_b_12_d_2), .H_2(cell_b_12_h_2));  // open: b_2
  Cell_B cell_b_13 (
    .Cout(cell_b_13_cout), .H(cell_b_17_h_2), .D(cell_b_17_d_2), .cin(cell_b_17_cout), .a(1'b0), .b(Y3),
    .b_2(cell_b_13_b_2), .z(cell_b_13_z), .D_2(cell_b_13_d_2), .H_2(cell_b_13_h_2));
  Cell_B cell_b_14 (
    .Cout(cell_b_14_cout), .H(cell_b_18_h_2), .D(cell_b_18_d_2), .cin(cell_b_18_cout), .a(cell_b_13_z),
    .b(cell_b_17_b_2), .b_2(cell_b_14_b_2), .z(cell_b_14_z), .D_2(cell_b_14_d_2), .H_2(cell_b_14_h_2));
  Cell_B cell_b_15 (
    .Cout(cell_b_15_cout), .H(cell_b_19_h_2), .D(cell_b_19_d_2), .cin(cell_b_19_cout), .a(cell_b_14_z),
    .b(cell_b_18_b_2), .b_2(cell_b_15_b_2), .z(cell_b_15_z), .D_2(cell_b_15_d_2), .H_2(cell_b_15_h_2));
  Cell_B cell_b_16 (
    .Cout(cell_b_16_cout), .H(cell_b_20_h_2), .D(cell_b_20_d_2), .cin(cell_b_20_cout), .a(cell_b_15_z),
    .b(cell_b_19_b_2), .z(P4), .D_2(cell_b_16_d_2), .H_2(cell_b_16_h_2));  // open: b_2
  Cell_B cell_b_17 (
    .Cout(cell_b_17_cout), .H(cell_b_21_h_2), .D(cell_b_21_d_2), .cin(cell_b_21_cout), .a(1'b0), .b(Y3),
    .b_2(cell_b_17_b_2), .z(cell_b_17_z), .D_2(cell_b_17_d_2), .H_2(cell_b_17_h_2));
  Cell_B cell_b_18 (
    .Cout(cell_b_18_cout), .H(cell_b_22_h_2), .D(cell_b_22_d_2), .cin(cell_b_22_cout), .a(cell_b_17_z),
    .b(cell_b_21_b_2), .b_2(cell_b_18_b_2), .z(cell_b_18_z), .D_2(cell_b_18_d_2), .H_2(cell_b_18_h_2));
  Cell_B cell_b_19 (
    .Cout(cell_b_19_cout), .H(cell_b_23_h_2), .D(cell_b_23_d_2), .cin(cell_b_23_cout), .a(cell_b_18_z),
    .b(cell_b_22_b_2), .b_2(cell_b_19_b_2), .z(cell_b_19_z), .D_2(cell_b_19_d_2), .H_2(cell_b_19_h_2));
  Cell_B cell_b_20 (
    .Cout(cell_b_20_cout), .H(cell_c_4_h), .D(cell_c_4_d), .cin(1'b0), .a(cell_b_19_z), .b(cell_b_23_b_2),
    .z(P3), .D_2(cell_b_20_d_2), .H_2(cell_b_20_h_2));  // open: b_2
  Cell_B cell_b_21 (
    .Cout(cell_b_21_cout), .H(cell_b_24_h_2), .D(cell_b_24_d_2), .cin(cell_b_24_cout), .a(1'b0), .b(Y2),
    .b_2(cell_b_21_b_2), .z(cell_b_21_z), .D_2(cell_b_21_d_2), .H_2(cell_b_21_h_2));
  Cell_B cell_b_22 (
    .Cout(cell_b_22_cout), .H(cell_b_25_h_2), .D(cell_b_25_d_2), .cin(cell_b_25_cout), .a(cell_b_21_z),
    .b(cell_b_24_b_2), .b_2(cell_b_22_b_2), .z(cell_b_22_z), .D_2(cell_b_22_d_2), .H_2(cell_b_22_h_2));
  Cell_B cell_b_23 (
    .Cout(cell_b_23_cout), .H(cell_c_3_h), .D(cell_c_3_d), .cin(1'b0), .a(cell_b_22_z), .b(cell_b_25_b_2),
    .b_2(cell_b_23_b_2), .z(P2), .D_2(cell_b_23_d_2), .H_2(cell_b_23_h_2));
  Cell_B cell_b_24 (
    .Cout(cell_b_24_cout), .H(cell_b_26_h_2), .D(cell_b_26_d_2), .cin(cell_b_26_cout), .a(1'b0), .b(Y1),
    .b_2(cell_b_24_b_2), .z(cell_b_24_z), .D_2(cell_b_24_d_2), .H_2(cell_b_24_h_2));
  Cell_B cell_b_25 (
    .Cout(cell_b_25_cout), .H(cell_c_2_h), .D(cell_c_2_d), .cin(1'b0), .a(cell_b_24_z), .b(cell_b_26_b_2),
    .b_2(cell_b_25_b_2), .z(P1), .D_2(cell_b_25_d_2), .H_2(cell_b_25_h_2));
  Cell_B cell_b_26 (
    .Cout(cell_b_26_cout), .H(cell_c_1_h), .D(cell_c_1_d), .cin(1'b0), .a(1'b0), .b(Y0), .b_2(cell_b_26_b_2),
    .z(P0), .D_2(cell_b_26_d_2), .H_2(cell_b_26_h_2));
  Cell_C cell_c_1 (.x_i_1(1'b0), .x_i(X0), .H(cell_c_1_h), .D(cell_c_1_d));
  Cell_C cell_c_2 (.x_i_1(X0), .x_i(X1), .H(cell_c_2_h), .D(cell_c_2_d));
  Cell_C cell_c_3 (.x_i_1(X1), .x_i(X2), .H(cell_c_3_h), .D(cell_c_3_d));
  Cell_C cell_c_4 (.x_i_1(X2), .x_i(X3), .H(cell_c_4_h), .D(cell_c_4_d));
endmodule
