// Logisim project Cse3105_lab_01_a.circ as structural Verilog: 1 circuit, main circuit main
module main (
  input  in_1,
  input  in_2,
  input  in_3,
  input  B,
  input  A,
  input  in_6,
  input  in_7,
  input  in_8,
  input  A_2,
  input  B_2,
  input  A_3,
  input  B_3,
  input  Cin,
  output out_14,
  output out_15,
  output \output ,
  output out_17,
  output out_18,
  output output_2,
  output Sum,
  output Cout
);

  wire and_1_out, and_2_out, pull_resistor_3_node, transistor_6_out, transistor_7_out, transistor_13_out,
       xor_1_out;

  Transistor #(.\type ("n")) transistor_1 (.in(1'b0), .out(\output ), .gate(A));
  Transistor transistor_2 (.in(1'b1), .out(out_17), .gate(in_6));
  Transistor #(.\type ("n")) transistor_3 (.in(1'b0), .out(output_2), .gate(A_2));
  Pull_Resistor #(.pull(1)) pull_resistor_1 (.node(out_15));
  Transistor #(.\type ("n")) transistor_4 (.in(1'b0), .out(out_15), .gate(in_2));
  Pull_Resistor #(.pull(1)) pull_resistor_2 (.node(\output ));
  Transistor #(.\type ("n")) transistor_5 (.in(transistor_6_out), .out(out_17), .gate(in_6));
  Transistor #(.\type ("n")) transistor_6 (.in(1'b0), .out(transistor_6_out), .gate(in_7));
  Pull_Resistor #(.pull(1)) pull_resistor_3 (.node(pull_resistor_3_node));
  Transistor transistor_7 (.in(pull_resistor_3_node), .out(transistor_7_out), .gate(A_2));
  Transistor transistor_8 (.in(transistor_7_out), .out(output_2), .gate(B_2));
  Transistor #(.\type ("n")) transistor_9 (.in(1'b0), .out(\output ), .gate(B));
  Transistor transistor_10 (.in(1'b1), .out(out_17), .gate(in_7));
  Transistor #(.\type ("n")) transistor_11 (.in(1'b0), .out(output_2), .gate(B_2));
  xor xor_1 (xor_1_out, A_3, B_3);
  and and_1 (and_1_out, A_3, B_3);
  xor xor_2 (Sum, xor_1_out, Cin);
  and and_2 (and_2_out, xor_1_out, Cin);
  Pull_Resistor #(.pull(1)) pull_resistor_4 (.node(out_14));
  Transistor #(.\type ("n")) transistor_12 (.in(transistor_13_out), .out(out_14), .gate(in_1));
  Transistor #(.\type ("n")) transistor_13 (.in(1'b0), .out(transistor_13_out), .gate(in_3));
  Pull_Resistor #(.pull(1)) pull_resistor_5 (.node(out_18));
  Transistor transistor_14 (.in(out_18), .out(out_18), .gate(in_8));
  Transistor #(.\type ("n")) transistor_15 (.in(1'b0), .out(out_18), .gate(in_8));
  or or_1 (Cout, and_2_out, and_1_out);

  // Notes on the sheet:
  //   NOT NMOS
  //   NOR CMOS
  //   NAND using CMOS
  //   NOR using NMOS
  //   Full Adder
  //   NAND NMOS
  //   pmos south nmos north
  //   NOT CMOS
endmodule
