// Logisim project EV2_2003015.circ as structural Verilog
module one_bit_register (
  input  Din,
  input  Scl,
  input  clk,
  output Dout
);

  wire multiplexer_1_out;

  Multiplexer multiplexer_1 (.in0(Dout), .in1(Din), .out(multiplexer_1_out), .sel(Scl));
  D_Flip_Flop d_ff_1 (.D(multiplexer_1_out), .clk(clk), .Q(Dout));  // open: Qn, preset, reset
endmodule

module flag (
  input  CF,
  input  SF,
  input  ZF,
  input  SEl,
  output CF_O,
  output SF_O,
  output ZF_O
);

  wire CLK_out;

  Clock CLK (.out(CLK_out));
  one_bit_register one_bit_register_1 (.Din(CF), .Scl(SEl), .clk(CLK_out), .Dout(CF_O));
  one_bit_register one_bit_register_2 (.Din(SF), .Scl(SEl), .clk(CLK_out), .Dout(SF_O));
  one_bit_register one_bit_register_3 (.Din(ZF), .Scl(SEl), .clk(CLK_out), .Dout(ZF_O));
endmodule

module bit4 (
  input  [3:0] Din,
  input  SEL,
  output [3:0] Dout
);

  wire CLK_out;

  Clock CLK (.out(CLK_out));
  one_bit_register one_bit_register_1 (.Din(Din[0]), .Scl(SEL), .clk(CLK_out), .Dout(Dout[0]));
  one_bit_register one_bit_register_2 (.Din(Din[1]), .Scl(SEL), .clk(CLK_out), .Dout(Dout[1]));
  one_bit_register one_bit_register_3 (.Din(Din[2]), .Scl(SEL), .clk(CLK_out), .Dout(Dout[2]));
  one_bit_register one_bit_register_4 (.Din(Din[3]), .Scl(SEL), .clk(CLK_out), .Dout(Dout[3]));
endmodule
