// Logisim project EV2_2003046.circ as structural Verilog: 5 circuits, main circuit one_bit_reg
module one_bit_reg (
  input  Din,
  input  SEL,
  input  CLK,
  output Dout
);

  wire multiplexer_1_out;

  Multiplexer multiplexer_1 (.in0(Dout), .in1(Din), .out(multiplexer_1_out), .sel(SEL));
  D_Flip_Flop d_ff_1 (.D(multiplexer_1_out), .clk(CLK), .Q(Dout));  // open: Qn, preset, reset
endmodule

module four_bit_reg (
  input  [3:0] Din,
  input  SEL,
  input  CLK,
  output [3:0] Dout
);

  one_bit_reg one_bit_reg_1 (.Din(Din[0]), .SEL(SEL), .CLK(CLK), .Dout(Dout[0]));
  one_bit_reg one_bit_reg_2 (.Din(Din[1]), .SEL(SEL), .CLK(CLK), .Dout(Dout[1]));
  one_bit_reg one_bit_reg_3 (.Din(Din[2]), .SEL(SEL), .CLK(CLK), .Dout(Dout[2]));
  one_bit_reg one_bit_reg_4 (.Din(Din[3]), .SEL(SEL), .CLK(CLK), .Dout(Dout[3]));
endmodule

module eight_bit_reg (
  input  [7:0] Din,
  input  SEL,
  input  CLK,
  output [7:0] Dout
);

  one_bit_reg one_bit_reg_1 (.Din(Din[0]), .SEL(SEL), .CLK(CLK), .Dout(Dout[0]));
  one_bit_reg one_bit_reg_2 (.Din(Din[1]), .SEL(SEL), .CLK(CLK), .Dout(Dout[1]));
  one_bit_reg one_bit_reg_3 (.Din(Din[2]), .SEL(SEL), .CLK(CLK), .Dout(Dout[2]));
  one_bit_reg one_bit_reg_4 (.Din(Din[3]), .SEL(SEL), .CLK(CLK), .Dout(Dout[3]));
  one_bit_reg one_bit_reg_5 (.Din(Din[4]), .SEL(SEL), .CLK(CLK), .Dout(Dout[4]));
  one_bit_reg one_bit_reg_6 (.Din(Din[5]), .SEL(SEL), .CLK(CLK), .Dout(Dout[5]));
  one_bit_reg one_bit_reg_7 (.Din(Din[6]), .SEL(SEL), .CLK(CLK), .Dout(Dout[6]));
  one_bit_reg one_bit_reg_8 (.Din(Din[7]), .SEL(SEL), .CLK(CLK), .Dout(Dout[7]));
endmodule

module Flag_reg (
  input  CF,
  input  SF,
  input  ZF,
  input  SEL,
  input  CLK,
  output CF_out,
  output SF_out,
  output ZF_out
);

  one_bit_reg one_bit_reg_1 (.Din(CF), .SEL(SEL), .CLK(CLK), .Dout(CF_out));
  one_bit_reg one_bit_reg_2 (.Din(SF), .SEL(SEL), .CLK(CLK), .Dout(SF_out));
  one_bit_reg one_bit_reg_3 (.Din(ZF), .SEL(SEL), .CLK(CLK), .Dout(ZF_out));
endmodule

module Sixteen_bit_reg (
  input  SEL,
  input  [15:0] Din,
  input  CLK,
  output [15:0] Dout
);

  eight_bit_reg eight_bit_reg_1 (.Din(Din[7:0]), .SEL(SEL), .CLK(CLK), .Dout(Dout[7:0]));
  eight_bit_reg eight_bit_reg_2 (.Din(Din[15:8]), .SEL(SEL), .CLK(CLK), .Dout(Dout[15:8]));
endmodule
