// Logisim project EV2_2003056.circ as structural Verilog: 5 circuits, main circuit one_bit_register
module one_bit_register (
  input  Din,
  input  Scl,
  input  clk,
  output Dout
);

  wire multiplexer_1_out;

  Multiplexer multiplexer_1 (.in0(Dout), .in1(Din), .out(multiplexer_1_out), .sel(Scl));
  D_Flip_Flop d_ff_1 (.D(multiplexer_1_out), .clk(clk), .Q(Dout));  // open: Qn, preset, reset
endmodule

module flag (
  input  CF,
  input  SF,
  input  ZF,
  input  SEl,
  output CF_O,
  output SF_O,
  output ZF_O
);

  wire CLK_out;

  Clock CLK (.out(CLK_out));
  one_bit_register one_bit_register_1 (.Din(CF), .Scl(SEl), .clk(CLK_out), .Dout(CF_O));
  one_bit_register one_bit_register_2 (.Din(SF), .Scl(SEl), .clk(CLK_out), .Dout(SF_O));
  one_bit_register one_bit_register_3 (.Din(ZF), .Scl(SEl), .clk(CLK_out), .Dout(ZF_O));
endmodule

module bit4 (
  input  [3:0] Din,
  input  SEL,
  output [3:0] Dout
);

  wire CLK_out;

  Clock CLK (.out(CLK_out));
  one_bit_register one_bit_register_1 (.Din(Din[0]), .Scl(SEL), .clk(CLK_out), .Dout(Dout[0]));
  one_bit_register one_bit_register_2 (.Din(Din[1]), .Scl(SEL), .clk(CLK_out), .Dout(Dout[1]));
  one_bit_register one_bit_register_3 (.Din(Din[2]), .Scl(SEL), .clk(CLK_out), .Dout(Dout[2]));
  one_bit_register one_bit_register_4 (.Din(Din[3]), .Scl(SEL), .clk(CLK_out), .Dout(Dout[3]));
endmodule

module bit8 (
  input  [7:0] Din,
  input  SEL,
  input  CLK,
  output [7:0] Dout
);

  one_bit_register one_bit_register_1 (.Din(Din[0]), .Scl(SEL), .clk(CLK), .Dout(Dout[0]));
  one_bit_register one_bit_register_2 (.Din(Din[1]), .Scl(SEL), .clk(CLK), .Dout(Dout[1]));
  one_bit_register one_bit_register_3 (.Din(Din[2]), .Scl(SEL), .clk(CLK), .Dout(Dout[2]));
  one_bit_register one_bit_register_4 (.Din(Din[3]), .Scl(SEL), .clk(CLK), .Dout(Dout[3]));
  one_bit_register one_bit_register_5 (.Din(Din[4]), .Scl(SEL), .clk(CLK), .Dout(Dout[4]));
  one_bit_register one_bit_register_6 (.Din(Din[5]), .Scl(SEL), .clk(CLK), .Dout(Dout[5]));
  one_bit_register one_bit_register_7 (.Din(Din[6]), .Scl(SEL), .clk(CLK), .Dout(Dout[6]));
  one_bit_register one_bit_register_8 (.Din(Din[7]), .Scl(SEL), .clk(CLK), .Dout(Dout[7]));
endmodule

module bit16 (
  input  [2:0] in_1,
  input  in_2
);

  wire decoder_1_out0, decoder_1_out1, decoder_1_out2, decoder_1_out3, decoder_1_out4, decoder_1_out5,
       decoder_1_out6, decoder_1_out7, decoder_1_out8, decoder_1_out9, decoder_1_out10, decoder_1_out11,
       decoder_1_out12, decoder_1_out13, undriven, undriven_2;

  Decoder #(.select(5)) decoder_1 (
    .out0(decoder_1_out0), .out1(decoder_1_out1), .out2(decoder_1_out2), .out3(decoder_1_out3),
    .out4(decoder_1_out4), .out5(decoder_1_out5), .out6(decoder_1_out6), .out7(decoder_1_out7),
    .out8(decoder_1_out8), .out9(decoder_1_out9), .out10(decoder_1_out10), .out11(decoder_1_out11),
    .out12(decoder_1_out12), .out13(decoder_1_out13));  // open: out14, out15, out16, out17, out18, out19, out20, out21, out22, out23, out24, out25, out26, out27, out28, out29, out30, out31, sel, en
  one_bit_register one_bit_register_1 (.Din(decoder_1_out0));  // open: Scl, clk, Dout
  one_bit_register one_bit_register_2 (.Din(decoder_1_out1));  // open: Scl, clk, Dout
  one_bit_register one_bit_register_3 (.Din(decoder_1_out2));  // open: Scl, clk, Dout
  one_bit_register one_bit_register_4 (.Din(decoder_1_out3));  // open: Scl, clk, Dout
  one_bit_register one_bit_register_5 (.Din(undriven_2));  // open: Scl, clk, Dout
  one_bit_register one_bit_register_6 (.Din(decoder_1_out4));  // open: Scl, clk, Dout
  one_bit_register one_bit_register_7 (.Din(decoder_1_out5));  // open: Scl, clk, Dout
  one_bit_register one_bit_register_8 (.Din(decoder_1_out6));  // open: Scl, clk, Dout
  one_bit_register one_bit_register_9 (.Din(decoder_1_out7));  // open: Scl, clk, Dout
  one_bit_register one_bit_register_10 (.Din(decoder_1_out8));  // open: Scl, clk, Dout
  one_bit_register one_bit_register_11 (.Din(decoder_1_out9));  // open: Scl, clk, Dout
  one_bit_register one_bit_register_12 (.Din(decoder_1_out10));  // open: Scl, clk, Dout
  one_bit_register one_bit_register_13 (.Din(decoder_1_out11));  // open: Scl, clk, Dout
  one_bit_register one_bit_register_14 (.Din(decoder_1_out12));  // open: Scl, clk, Dout
  one_bit_register one_bit_register_15 (.Din(undriven));  // open: Scl, clk, Dout
  one_bit_register one_bit_register_16 ();  // open: Din, Scl, clk, Dout
endmodule
