// Logisim project fulladdercircuitversion.circ as structural Verilog: 2 circuits, main circuit Full_Adder
module Full_Adder (
  input  in_1,
  input  in_2,
  input  in_3,
  output out_4,
  output out_5
);

  wire and_1_out, and_2_out, xor_1_out;

  xor xor_1 (xor_1_out, in_1, in_2);
  and and_1 (and_1_out, in_1, in_2);
  xor xor_2 (out_4, xor_1_out, in_3);
  and and_2 (and_2_out, xor_1_out, in_3);
  or or_1 (out_5, and_2_out, and_1_out);

  // Notes on the sheet:
  //   Full Adder
endmodule

module fulladder (
  input  [3:0] in_1,
  input  in_2,
  input  [3:0] in_3,
  output out_4,
  output out_5,
  output out_6,
  output out_7,
  output out_8
);

  wire full_adder_1_out_5, full_adder_2_out_5, full_adder_3_out_5;

  Full_Adder full_adder_1 (.in_1(in_1[3]), .in_2(in_3[3]), .in_3(in_2), .out_4(out_6), .out_5(full_adder_1_out_5));
  Full_Adder full_adder_2 (
    .in_1(in_1[2]), .in_2(in_3[3]), .in_3(full_adder_1_out_5), .out_4(out_7), .out_5(full_adder_2_out_5));
  Full_Adder full_adder_3 (
    .in_1(in_1[1]), .in_2(in_3[3]), .in_3(full_adder_2_out_5), .out_4(out_4), .out_5(full_adder_3_out_5));
  Full_Adder full_adder_4 (.in_1(in_1[0]), .in_2(in_3[3]), .in_3(full_adder_3_out_5), .out_4(out_5), .out_5(out_8));

  assign in_3[2:0] = {3{in_3[3]}};
endmodule
