// Logisim project nmos_cir.circ as structural Verilog: 2 circuits, main circuit main
module main (
  input  A,
  input  B,
  input  C,
  input  in_4,
  input  in_5,
  input  in_6,
  output A_prime_BC,
  output out_8
);

  wire pull_resistor_1_node, pull_resistor_2_node, pull_resistor_3_node, pull_resistor_4_node,
       pull_resistor_5_node, pull_resistor_6_node, transistor_3_out, transistor_7_out, transistor_8_out,
       transistor_9_out, transistor_12_out, transistor_14_out, transistor_20_out;

  Pull_Resistor #(.pull(1)) pull_resistor_1 (.node(pull_resistor_1_node));
  Transistor #(.\type ("n")) transistor_1 (.in(1'b0), .out(pull_resistor_1_node), .gate(A));
  Pull_Resistor #(.pull(1)) pull_resistor_2 (.node(pull_resistor_2_node));
  Transistor #(.\type ("n")) transistor_2 (.in(1'b0), .out(pull_resistor_2_node), .gate(pull_resistor_1_node));
  Pull_Resistor #(.pull(1)) pull_resistor_3 (.node(pull_resistor_3_node));
  Transistor transistor_3 (.in(pull_resistor_3_node), .out(transistor_3_out), .gate(in_6));
  Transistor #(.\type ("n")) transistor_4 (.in(1'b0), .out(transistor_3_out), .gate(in_6));
  Transistor #(.\type ("n")) transistor_5 (.in(1'b0), .out(pull_resistor_2_node), .gate(pull_resistor_5_node));
  Pull_Resistor #(.pull(1)) pull_resistor_4 (.node(pull_resistor_4_node));
  Transistor #(.\type ("n")) transistor_6 (.in(transistor_7_out), .out(pull_resistor_4_node), .gate(B));
  Transistor #(.\type ("n")) transistor_7 (.in(1'b0), .out(transistor_7_out), .gate(C));
  Transistor transistor_8 (.in(pull_resistor_3_node), .out(transistor_8_out), .gate(transistor_3_out));
  Transistor transistor_9 (.in(transistor_8_out), .out(transistor_9_out), .gate(transistor_20_out));
  Transistor #(.\type ("n")) transistor_10 (.in(1'b0), .out(transistor_9_out), .gate(transistor_3_out));
  Pull_Resistor #(.pull(1)) pull_resistor_5 (.node(pull_resistor_5_node));
  Transistor #(.\type ("n")) transistor_11 (.in(1'b0), .out(pull_resistor_5_node), .gate(pull_resistor_4_node));
  Pull_Resistor #(.pull(1)) pull_resistor_6 (.node(pull_resistor_6_node));
  Transistor transistor_12 (.in(pull_resistor_6_node), .out(transistor_12_out), .gate(in_4));
  Transistor #(.\type ("n")) transistor_13 (.in(transistor_14_out), .out(transistor_12_out), .gate(in_4));
  Transistor #(.\type ("n")) transistor_14 (.in(1'b0), .out(transistor_14_out), .gate(in_5));
  Transistor #(.\type ("n")) transistor_15 (.in(1'b0), .out(transistor_9_out), .gate(transistor_20_out));
  Pull_Resistor #(.pull(1)) pull_resistor_7 (.node(A_prime_BC));
  Transistor #(.\type ("n")) transistor_16 (.in(1'b0), .out(A_prime_BC), .gate(pull_resistor_2_node));
  Transistor transistor_17 (.in(pull_resistor_6_node), .out(transistor_12_out), .gate(in_5));
  Transistor transistor_18 (.in(pull_resistor_3_node), .out(out_8), .gate(transistor_9_out));
  Transistor #(.\type ("n")) transistor_19 (.in(1'b0), .out(out_8), .gate(transistor_9_out));
  Transistor transistor_20 (.in(pull_resistor_3_node), .out(transistor_20_out), .gate(transistor_12_out));
  Transistor #(.\type ("n")) transistor_21 (.in(1'b0), .out(transistor_20_out), .gate(transistor_12_out));

  // Notes on the sheet:
  //   A'
  //   BC
endmodule

module cir1 (
  input  in_1,
  input  in_2,
  input  in_3,
  output out_4
);

  main main_1 (.A(in_1), .B(in_2), .C(in_3), .in_4(in_3), .in_5(in_3), .A_prime_BC(out_4));  // open: in_6, out_8
endmodule
