// Logisim project sram1_1.circ as structural Verilog: 3 circuits, main circuit main
module main (
  input  rs1,
  input  rs2,
  input  wd,
  input  ws,
  input  clk,
  output rd1,
  output rd2
);

  wire d_ff_1_q, multiplexer_1_out;

  Multiplexer multiplexer_1 (.in0(d_ff_1_q), .in1(wd), .out(multiplexer_1_out), .sel(ws));
  D_Flip_Flop d_ff_1 (.D(multiplexer_1_out), .clk(clk), .Q(d_ff_1_q));  // open: Qn, preset, reset
  and and_1 (rd1, rs1, d_ff_1_q);
  and and_2 (rd2, rs2, d_ff_1_q);
endmodule

module Sram11 (
  input  ws,
  input  [2:0] wd,
  input  clk,
  input  rs1,
  input  rs2,
  output [2:0] rd1,
  output [2:0] rd2
);

  main main_1 (.rs1(rs1), .rs2(rs2), .wd(wd[0]), .ws(ws), .clk(clk), .rd1(rd1[0]), .rd2(rd2[0]));
  main main_2 (.rs1(rs1), .rs2(rs2), .wd(wd[1]), .ws(ws), .clk(clk), .rd1(rd1[1]), .rd2(rd2[1]));
  main main_3 (.rs1(rs1), .rs2(rs2), .wd(wd[2]), .ws(ws), .clk(clk), .rd1(rd1[2]), .rd2(rd2[2]));
endmodule

module sram43 (
);

  Sram11 sram11_1 ();  // open: ws, wd, clk, rs1, rs2, rd1, rd2
  Sram11 sram11_2 ();  // open: ws, wd, clk, rs1, rs2, rd1, rd2
  Sram11 sram11_3 ();  // open: ws, wd, clk, rs1, rs2, rd1, rd2
  Sram11 sram11_4 ();  // open: ws, wd, clk, rs1, rs2, rd1, rd2
endmodule
